// Logisim project countdown_timer.circ as structural Verilog: 1 circuit, main circuit main
module main (
);

  wire and_1_out, and_2_out, and_3_out, and_4_out, and_5_out, and_6_out, and_7_out, clock_1_out, Enable_out,
       j_k_ff_1_qn, j_k_ff_2_qn, j_k_ff_3_qn, j_k_ff_4_qn, j_k_ff_5_qn, j_k_ff_6_qn, j_k_ff_7_qn,
       j_k_ff_8_qn, nor_1_out, nor_2_out, nor_3_out, not_1_out, not_2_out, not_3_out, not_4_out, not_5_out,
       not_6_out, not_7_out, not_8_out, PauseResume_out, Reset_out;
  wire [2:0] j_k_ff_3_q;
  wire [3:0] j_k_ff_2_q;

  Clock clock_1 (.out(clock_1_out));
  LED Paused (.in(j_k_ff_1_qn));
  Button #(.press("passive")) PauseResume (.out(PauseResume_out));
  Button #(.press("passive")) Reset (.out(Reset_out));
  and and_1 (and_1_out, j_k_ff_3_qn, j_k_ff_5_qn, j_k_ff_7_qn);
  and and_2 (and_2_out, and_1_out, j_k_ff_2_qn, and_3_out);
  and and_3 (and_3_out, j_k_ff_4_qn, j_k_ff_6_qn, j_k_ff_8_qn);
  J_K_Flip_Flop #(.trigger("falling")) j_k_ff_1 (
    .J(1'b1), .K(1'b1), .clk(PauseResume_out), .Qn(j_k_ff_1_qn), .reset(not_1_out));  // open: Q, preset
  not not_1 (not_1_out, Reset_out);
  J_K_Flip_Flop j_k_ff_2 (
    .J(Reset_out), .K(Reset_out), .clk(Enable_out), .Q(j_k_ff_2_q[0]), .Qn(j_k_ff_2_qn), .reset(not_2_out));  // open: preset
  not not_2 (not_2_out, Reset_out);
  J_K_Flip_Flop #(.trigger("falling")) j_k_ff_3 (
    .J(1'b1), .K(1'b1), .clk(nor_2_out), .Q(j_k_ff_3_q[0]), .Qn(j_k_ff_3_qn), .reset(not_3_out));  // open: preset
  not not_3 (not_3_out, Reset_out);
  J_K_Flip_Flop j_k_ff_4 (
    .J(j_k_ff_2_qn), .K(j_k_ff_2_qn), .clk(Enable_out), .Q(j_k_ff_2_q[1]), .Qn(j_k_ff_4_qn), .reset(not_4_out));  // open: preset
  J_K_Flip_Flop #(.trigger("falling")) j_k_ff_5 (
    .J(j_k_ff_3_qn), .K(j_k_ff_3_qn), .clk(nor_2_out), .Q(j_k_ff_3_q[1]), .Qn(j_k_ff_5_qn), .preset(not_5_out));  // open: reset
  nor nor_1 (nor_1_out, j_k_ff_1_qn, and_2_out);
  not not_4 (not_4_out, nor_2_out);
  not not_5 (not_5_out, Reset_out);
  and and_4 (and_4_out, j_k_ff_5_qn, j_k_ff_3_qn);
  and Enable (Enable_out, clock_1_out, nor_1_out);
  and and_5 (and_5_out, j_k_ff_2_qn, j_k_ff_4_qn);
  J_K_Flip_Flop j_k_ff_6 (
    .J(and_5_out), .K(and_5_out), .clk(Enable_out), .Q(j_k_ff_2_q[2]), .Qn(j_k_ff_6_qn), .reset(not_6_out));  // open: preset
  not not_6 (not_6_out, nor_2_out);
  nor nor_2 (nor_2_out, and_7_out, nor_3_out);
  not not_7 (not_7_out, Reset_out);
  J_K_Flip_Flop #(.trigger("falling")) j_k_ff_7 (
    .J(and_4_out), .K(and_4_out), .clk(nor_2_out), .Q(j_k_ff_3_q[2]), .Qn(j_k_ff_7_qn), .preset(not_7_out));  // open: reset
  and and_6 (and_6_out, and_5_out, j_k_ff_6_qn);
  J_K_Flip_Flop j_k_ff_8 (
    .J(and_6_out), .K(and_6_out), .clk(Enable_out), .Q(j_k_ff_2_q[3]), .Qn(j_k_ff_8_qn), .reset(not_8_out));  // open: preset
  nor nor_3 (nor_3_out, Reset_out, Reset_out);
  not not_8 (not_8_out, Reset_out);
  and and_7 (and_7_out, j_k_ff_2_q[2], j_k_ff_2_q[3]);
  Hex_Digit_Display #(.decimalPoint("false")) hex_digit_display_1 (.value({1'b0, j_k_ff_3_q}));
  Hex_Digit_Display #(.decimalPoint("false")) hex_digit_display_2 (.value(j_k_ff_2_q));

  // Notes on the sheet:
  //   10s place
  //   1s place
endmodule
